# Fritzing sketch project1_schema_DenizKahriman_0984809 (saved by Fritzing 0.9.3b)
perfboards: 1

parts:
  Part4 = Arduino Uno (Rev3)
  U2 = 74HC4052 [package=dil16]
  R1 = Resistor [tolerance=±5% resistance=220 package=THT]  # not connected
  R2 = Resistor [tolerance=±5% resistance=220 package=THT]
  R3 = Resistor [tolerance=±5% resistance=220 package=THT]
  R4 = Resistor [tolerance=±5% resistance=220 package=THT]
  R5 = Resistor [tolerance=±5% resistance=220 package=THT]
  LED1 = LED - 5mm [color="Red (633nm)" package="5 mm [THT]"]
  7_Segment1 = 7 Segment Display
  S1 = Pushbutton [package="[THT]"]
  S2 = Pushbutton [package="[THT]"]
  S3 = Reed switch [package=THT]  # not connected
  LED3 = LEDs [package=led10mm]
  LED4 = LED - 5mm [color="Red (633nm)" package="5 mm [THT]"]

nets:
  N1: Part4.D8, R2.Pin_1
  N2: Part4.D10_PWM/SS, U2.X3
  N3: Part4.D11_PWM/MOSI, U2.X1
  N4: Part4.D12/MISO, U2.X0
  N5: Part4.D2, S2.Pin_3
  N6: Part4.D3_PWM, LED4.anode
  N7: Part4.D4, S1.Pin_3, S1.Pin_4
  N8: Part4.D5_PWM, LED3.A
  N9: Part4.D7, LED1.anode
  N10: U2.Y0, 7_Segment1.Segment_A
  N11: U2.Y2, 7_Segment1.Segment_B
  N12: U2.Y, 7_Segment1.Segment_C
  N13: U2.Y3, 7_Segment1.Segment_DP
  N14: U2.Y1, 7_Segment1.Segment_F
  N15: U2.INH, 7_Segment1.Segment_E
  N16: U2.VEE, 7_Segment1.Segment_D
  N17: R3.Pin_1, LED4.cathode
  N18: R4.Pin_1, LED1.cathode
  N19: R5.Pin_1, 7_Segment1.common_anode
