# Fritzing sketch Drawing (saved by Fritzing 0.9.3b)
breadboards: 1

parts:
  arduino = Arduino Uno (Rev3)
  U2 = 74HC595 [package="DIP16 [THT]"]
  7_Segment2 = 7 Segment Display
  S1 = Pushbutton [package="[THT]"]
  S2 = Pushbutton [package="[THT]"]
  LED1 = LED - 5mm [color="Red (633nm)" package="5 mm [THT]"]
  LED2 = LED - 5mm [color="White (6500K)" package="5 mm [THT]"]
  LED3 = LED - 5mm [color="Red (633nm)" package="5 mm [THT]"]  # not connected
  R1 = Resistor [tolerance=±5% resistance=1k package=THT]  # not connected
  R2 = Resistor [tolerance=±5% resistance=1k package=THT]  # not connected
  R3 = Resistor [tolerance=±5% resistance=220 package=THT]

nets:
  N1: arduino.A0, S2.Pin_3, S2.Pin_4
  N2: arduino.A1, LED2.cathode
  N3: arduino.A2, S1.Pin_3, S1.Pin_4
  N4: arduino.A3, LED1.cathode
  N5: arduino.D9_PWM, R3.Pin_1
  N6: arduino.D10_PWM/SS, U2.SH_CP
  N7: arduino.D11_PWM/MOSI, U2.DS
  N8: arduino.D12/MISO, U2.ST_CP
  5V: arduino.5V, U2.MR, U2.VCC
  GND: arduino.GND, U2.GND, U2.OE, 7_Segment2.common_cathode, S1.Pin_1, S1.Pin_2, S2.Pin_1, S2.Pin_2
  N9: U2.Q1, 7_Segment2.Segment_A#1
  N10: U2.Q2, 7_Segment2.Segment_F
  N11: U2.Q3, 7_Segment2.Segment_E
  N12: U2.Q4, 7_Segment2.Segment_D
  N13: U2.Q5, 7_Segment2.Segment_C
  N14: U2.Q6, 7_Segment2.Segment_B
  N15: U2.Q7, 7_Segment2.Segment_A#10
  N16: U2.Q0, 7_Segment2.Segment_DP

// code stored in the sketch: shift out.ino
#define clockPin 10 // pin connected to SRCLK of 74HC595 
#define dataPin 11 // pin connected to SER of 74HC595 
#define latchPin 12 // pin connected to RCLK of 74HC595

const byte datArray[] = {
  B10000001,  // 0
  B11110011,  // 1
  B01001001,  // 2
  B01100001,  // 3
  B00110011,  // 4
  B00100101,  // 5
  B00000101,  // 6
  B11110001,  // 7
  B00000001,  // 8
  B00100001   // 9
};

void setup() {
  pinMode(latchPin, OUTPUT);
  pinMode(clockPin, OUTPUT);
  pinMode(dataPin, OUTPUT);
}

void writeDigit(int i) {
  digitalWrite(latchPin, LOW); // latchPin low for duration of transmission
  shiftOut(dataPin, clockPin, MSBFIRST, datArray[i]); // send data
  digitalWrite(latchPin, HIGH); // latchPin high to save the data
}

void loop() {
  for (int i = 0; i < 10; i++) {
    writeDigit(i);
    delay(500);
  }
}
